// Logisim project cpu.circ as structural Verilog: 3 circuits, main circuit main
module main (
);

  wire alu_1_zero, and_1_out, CLK_out, xor_1_out;
  wire [2:0] rom_1_data_3;
  wire [3:0] alu_1_aluout, multiplexer_1_out, multiplexer_2_out, multiplexer_3_out, ram_1_dout,
       registers_1_read_data_a, registers_1_read_data_b, rom_1_data;
  wire [7:0] adder_1_out, adder_2_out, bit_extender_1_out, Instruction_Counter_q, multiplexer_4_out,
       multiplexer_5_out;
  wire [12:4] rom_1_data_2;
  wire [15:0] Instruction_Memory_data;

  Clock CLK (.out(CLK_out));
  Register #(.trigger("falling")) Instruction_Counter (
    .D(multiplexer_5_out), .en(1'b1), .clk(CLK_out), .Q(Instruction_Counter_q));  // open: clr
  Adder adder_1 (.a(Instruction_Counter_q), .b(8'h1), .out(adder_1_out));  // open: cin, cout
  ROM #(.dataWidth(16)) Instruction_Memory (.addr(Instruction_Counter_q), .data(Instruction_Memory_data));
  ROM #(.addrWidth(4), .dataWidth(16)) rom_1 (
    .addr(Instruction_Memory_data[15:12]), .data({rom_1_data_3, rom_1_data_2, rom_1_data}));
  Multiplexer #(.width(4)) multiplexer_1 (
    .in0(Instruction_Memory_data[7:4]), .in1(Instruction_Memory_data[3:0]), .out(multiplexer_1_out),
    .sel(rom_1_data_2[11]));
  Registers registers_1 (
    .RegWrite(rom_1_data_2[12]), .read_reg_A(Instruction_Memory_data[11:8]),
    .read_reg_B(Instruction_Memory_data[7:4]), .write_reg(multiplexer_1_out), .write_data(multiplexer_3_out),
    .CLK(CLK_out), .read_data_A(registers_1_read_data_a), .read_data_B(registers_1_read_data_b));
  Multiplexer #(.width(4)) multiplexer_2 (
    .in0(registers_1_read_data_b), .in1(Instruction_Memory_data[3:0]), .out(multiplexer_2_out),
    .sel(rom_1_data_2[10]));
  ALU alu_1 (
    .A(registers_1_read_data_a), .B(multiplexer_2_out), .Control(rom_1_data_3), .ALUout(alu_1_aluout),
    .zero(alu_1_zero));
  assign bit_extender_1_out = {{4{Instruction_Memory_data[3]}}, Instruction_Memory_data[3:0]};  // Bit_Extender bit_extender_1
  RAM #(.addrWidth(4), .dataWidth(4)) ram_1 (
    .addr(alu_1_aluout), .we(rom_1_data_2[9]), .oe(rom_1_data_2[8]), .clk(CLK_out),
    .din(registers_1_read_data_b), .dout(ram_1_dout));
  Adder adder_2 (.a(adder_1_out), .b(bit_extender_1_out), .out(adder_2_out));  // open: cin, cout
  xor xor_1 (xor_1_out, rom_1_data_2[6], alu_1_zero);
  and and_1 (and_1_out, rom_1_data_2[5], xor_1_out);
  Multiplexer #(.width(4)) multiplexer_3 (
    .in0(alu_1_aluout), .in1(ram_1_dout), .out(multiplexer_3_out), .sel(rom_1_data_2[7]));
  Multiplexer #(.width(8)) multiplexer_4 (
    .in0(adder_1_out), .in1(adder_2_out), .out(multiplexer_4_out), .sel(and_1_out));
  Multiplexer #(.width(8)) multiplexer_5 (
    .in0(multiplexer_4_out), .in1(Instruction_Memory_data[11:4]), .out(multiplexer_5_out),
    .sel(rom_1_data_2[4]));

  // Notes on the sheet:
  //   contents of Instruction_Memory (hex, n*v repeats v):
  //   406f 4016 6610 4661 d661 f620
  //   Opcode
  //   contents of rom_1 (hex, n*v repeats v):
  //   2020 1800 9800 7800 1400 b800 600 3800 10 5800 d800 7400 2060 3400 5400 1580
  //   RegWrite
  //   ALUop
endmodule

module Registers (
  input  RegWrite,
  input  [3:0] read_reg_A,
  input  [3:0] read_reg_B,
  input  [3:0] write_reg,
  input  [3:0] write_data,
  input  CLK,
  output [3:0] read_data_A,
  output [3:0] read_data_B
);

  wire decoder_1_out1, decoder_1_out2, decoder_1_out3, decoder_1_out4, decoder_1_out5, decoder_1_out6;
  wire [3:0] sp_q, t0_q, t1_q, t2_q, t3_q, t4_q, zero_q;

  Decoder #(.select(4)) decoder_1 (
    .out1(decoder_1_out1), .out2(decoder_1_out2), .out3(decoder_1_out3), .out4(decoder_1_out4),
    .out5(decoder_1_out5), .out6(decoder_1_out6), .sel(write_reg), .en(RegWrite));  // open: out0, out7, out8, out9, out10, out11, out12, out13, out14, out15
  Register #(.trigger("falling"), .width(4)) zero (.D(4'b0000), .en(1'b0), .clk(CLK), .Q(zero_q));  // open: clr
  Register #(.trigger("falling"), .width(4)) t0 (
    .D(write_data), .en(decoder_1_out1), .clk(CLK), .Q(t0_q));  // open: clr
  Register #(.trigger("falling"), .width(4)) t1 (
    .D(write_data), .en(decoder_1_out2), .clk(CLK), .Q(t1_q));  // open: clr
  Register #(.trigger("falling"), .width(4)) t2 (
    .D(write_data), .en(decoder_1_out3), .clk(CLK), .Q(t2_q));  // open: clr
  Register #(.trigger("falling"), .width(4)) t3 (
    .D(write_data), .en(decoder_1_out4), .clk(CLK), .Q(t3_q));  // open: clr
  Register #(.trigger("falling"), .width(4)) t4 (
    .D(write_data), .en(decoder_1_out5), .clk(CLK), .Q(t4_q));  // open: clr
  Register #(.trigger("falling"), .width(4)) sp (
    .D(write_data), .en(decoder_1_out6), .clk(CLK), .Q(sp_q));  // open: clr
  Multiplexer #(.select(4), .width(4)) multiplexer_1 (
    .in0(zero_q), .in1(t0_q), .in2(t1_q), .in3(t2_q), .in4(t3_q), .in5(t4_q), .in6(sp_q), .out(read_data_A),
    .sel(read_reg_A));  // open: in7, in8, in9, in10, in11, in12, in13, in14, in15
  Multiplexer #(.select(4), .width(4)) multiplexer_2 (
    .in0(zero_q), .in1(t0_q), .in2(t1_q), .in3(t2_q), .in4(t3_q), .in5(t4_q), .in6(sp_q), .out(read_data_B),
    .sel(read_reg_B));  // open: in7, in8, in9, in10, in11, in12, in13, in14, in15
endmodule

module ALU (
  input  [3:0] A,
  input  [3:0] B,
  input  [2:0] Control,
  output [3:0] ALUout,
  output zero
);

  wire or_2_out;
  wire [3:0] adder_1_out, and_1_out, multiplexer_1_out, multiplexer_2_out, nor_1_out, or_1_out,
       shifter_1_out, shifter_2_out, subtractor_1_out;

  Adder #(.width(4)) adder_1 (.a(A), .b(B), .out(adder_1_out));  // open: cin, cout
  Subtractor #(.width(4)) subtractor_1 (.a(A), .b(B), .out(subtractor_1_out));  // open: bin, bout
  assign and_1_out = A & B;  // AND_Gate and_1, 4 bits wide
  assign or_1_out = A | B;  // OR_Gate or_1, 4 bits wide
  assign nor_1_out = ~(A | B);  // NOR_Gate nor_1, 4 bits wide
  or or_2 (or_2_out, B[2], B[3]);
  Shifter #(.width(4)) shifter_1 (.in(A), .\dist (B[1:0]), .out(shifter_1_out));
  Shifter #(.shift("lr"), .width(4)) shifter_2 (.in(A), .\dist (B[1:0]), .out(shifter_2_out));
  Multiplexer #(.width(4)) multiplexer_1 (.in0(shifter_1_out), .in1(4'b0000), .out(multiplexer_1_out), .sel(or_2_out));
  Multiplexer #(.width(4)) multiplexer_2 (.in0(shifter_2_out), .in1(4'b0000), .out(multiplexer_2_out), .sel(or_2_out));
  Multiplexer #(.select(3), .width(4)) multiplexer_3 (
    .in0(adder_1_out), .in1(subtractor_1_out), .in2(and_1_out), .in3(or_1_out), .in4(nor_1_out),
    .in5(multiplexer_1_out), .in6(multiplexer_2_out), .out(ALUout), .sel(Control));  // open: in7
  nor nor_2 (zero, ALUout[0], ALUout[1], ALUout[2], ALUout[3]);
endmodule
